# Fritzing sketch Circuit Design ESP8266-Huzzah (saved by Fritzing 0.9.3b)
breadboards: 1

parts:
  IC1 = L293D [package=THT]
  Adafruit_HUZZAH_ESP8266 = Adafruit HUZZAH ESP8266 Breakout [part_number=2471]
  Bat1 = battery_holder_dual_18650 [part_number=TBH-18650-2A-P]
  RM = DC Motor
  LM = DC Motor
  U1 = Voltage Regulator -- 3.3 V -- LM1117
  C2 = Electrolytic Capacitor [capacitance=100μF package="0807 [SMD, electrolytic]"]
  C3 = Electrolytic Capacitor [capacitance=100μF package="0807 [SMD, electrolytic]"]
  U2 = Voltage Regulator - 5V [package="TO220 [THT]"]

nets:
  N1: IC1.Enable_1, Adafruit_HUZZAH_ESP8266.#16
  N2: IC1.In_1, Adafruit_HUZZAH_ESP8266.#12
  N3: IC1.Out_1_(_Controlled_by_Enable_1_), LM.pin_2
  GND: IC1.0V, Adafruit_HUZZAH_ESP8266.GND, Bat1.+#1, U1.GND, C2.-, C3.-, U2.GND
  N4: IC1.Out_2_(_Controlled_by_Enable_1_), LM.pin_1
  N5: IC1.In_2, Adafruit_HUZZAH_ESP8266.#13
  N6: IC1.+Vmotor, C2.+, U2.output_voltage
  N7: IC1.Enable_2, Adafruit_HUZZAH_ESP8266.#5
  N8: IC1.In_3, Adafruit_HUZZAH_ESP8266.#15
  N9: IC1.Out_3_(_Controlled_by_Enable_2_), RM.pin_2
  N10: IC1.Out_4_(_Controlled_by_Enable_2_), RM.pin_1
  N11: IC1.In_4, Adafruit_HUZZAH_ESP8266.#4
  N12: IC1.+V, Adafruit_HUZZAH_ESP8266.VBat, U1.OUT, C3.+
  N13: Bat1.+#0, Bat1.+#2
  N14: Bat1.+#3, U1.IN, U2.input_voltage

custom parts:
  battery_holder_dual_18650: TBH-18650-2A-P dual 18650 battery holder.
  Voltage Regulator -- 3.3 V -- LM1117: LM1117-3.3 Voltage regulator, 3.3 V output. Note that the pinout order is not the same as LM7805 or LM7833.

// code stored in the sketch: Untitled2.ino

