# Fritzing sketch Circuit Design ESP8266 (saved by Fritzing 0.9.3b)
breadboards: 1

parts:
  IC1 = L293D [package=THT]
  Adafruit_HUZZAH_ESP8266 = Adafruit HUZZAH ESP8266 Breakout [part_number=2471]
  Bat1 = battery_holder_dual_18650 [part_number=TBH-18650-2A-P]
  RM = DC Motor
  LM = DC Motor

nets:
  N1: IC1.Enable_1, IC1.+Vmotor, IC1.Enable_2, IC1.+V, Adafruit_HUZZAH_ESP8266.VBat, Bat1.+#3
  N2: IC1.In_1, Adafruit_HUZZAH_ESP8266.#12
  N3: IC1.Out_1_(_Controlled_by_Enable_1_), LM.pin_2
  N4: IC1.0V, Adafruit_HUZZAH_ESP8266.GND, Bat1.+#1
  N5: IC1.Out_2_(_Controlled_by_Enable_1_), LM.pin_1
  N6: IC1.In_2, Adafruit_HUZZAH_ESP8266.#14
  N7: IC1.In_3, Adafruit_HUZZAH_ESP8266.#5
  N8: IC1.Out_3_(_Controlled_by_Enable_2_), RM.pin_2
  N9: IC1.Out_4_(_Controlled_by_Enable_2_), RM.pin_1
  N10: IC1.In_4, Adafruit_HUZZAH_ESP8266.#4
  N11: Bat1.+#0, Bat1.+#2

custom parts:
  battery_holder_dual_18650: TBH-18650-2A-P dual 18650 battery holder.
