# Fritzing sketch Circuit Design Feather ESP8266 (saved by Fritzing 0.9.3b)
breadboards: 1

parts:
  IC1 = L293D [package=THT]
  Bat1 = battery_holder_dual_18650 [part_number=TBH-18650-2A-P]
  RM = DC Motor
  LM = DC Motor
  Componente1 = Adafruit Feather HUZZAH ESP8266 [part_number="Adafruit #2821"]

nets:
  N1: IC1.Enable_1, IC1.+Vmotor, IC1.Enable_2, IC1.+V, Bat1.+#3, Componente1.VBAT
  N2: IC1.In_1, Componente1.GPIO12/MISO
  N3: IC1.Out_1_(_Controlled_by_Enable_1_), LM.pin_2
  N4: IC1.0V, Bat1.+#1, Componente1.GND
  N5: IC1.Out_2_(_Controlled_by_Enable_1_), LM.pin_1
  N6: IC1.In_2, Componente1.GPIO14/SCK
  N7: IC1.In_3, Componente1.GPIO5/SCL
  N8: IC1.Out_3_(_Controlled_by_Enable_2_), RM.pin_2
  N9: IC1.Out_4_(_Controlled_by_Enable_2_), RM.pin_1
  N10: IC1.In_4, Componente1.GPIO4/SDA
  N11: Bat1.+#0, Bat1.+#2

custom parts:
  battery_holder_dual_18650: TBH-18650-2A-P dual 18650 battery holder.
  Adafruit Feather HUZZAH ESP8266: his is the Adafruit Feather HUZZAH ESP8266 - our take on an 'all-in-one' ESP8266 WiFi development board with built in USB and battery charging. Its an ESP8266 WiFi module with all the extras you need, ready to rock! We have other boards in the Feather family, check'em out here. At the Feather HUZZAH's heart is an ESP8266 WiFi microcontroller clocked at 80 MHz and at 3.3V logic. This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
