# Fritzing sketch Circuit Design NodeMCU ESP8266 (saved by Fritzing 0.9.3b)
breadboards: 1

parts:
  IC1 = L293D [package=THT]
  Bat1 = battery_holder_dual_18650 [part_number=TBH-18650-2A-P]
  RM = DC Motor
  LM = DC Motor
  U1 = Voltage Regulator -- 3.3 V -- LM1117
  U2 = NodeMCU V1.0
  U3 = Voltage Regulator - 5V [package="TO220 [THT]"]
  C3 = Electrolytic Capacitor [capacitance=100μF package="0807 [SMD, electrolytic]"]
  C4 = Electrolytic Capacitor [capacitance=100μF package="0807 [SMD, electrolytic]"]

nets:
  N1: IC1.Enable_1, U2.D6
  N2: IC1.In_1, U2.D5
  N3: IC1.Out_1_(_Controlled_by_Enable_1_), LM.pin_2
  GND: IC1.0V, Bat1.+#1, U1.GND, U2.GND, U3.GND, C3.-, C4.-
  N4: IC1.Out_2_(_Controlled_by_Enable_1_), LM.pin_1
  N5: IC1.In_2, U2.D7
  N6: IC1.+Vmotor, U3.output_voltage, C3.+
  N7: IC1.Enable_2, U2.D2
  N8: IC1.In_3, U2.D3
  N9: IC1.Out_3_(_Controlled_by_Enable_2_), RM.pin_2
  N10: IC1.Out_4_(_Controlled_by_Enable_2_), RM.pin_1
  N11: IC1.In_4, U2.D1
  N12: IC1.+V, U1.OUT, U2.3V3, C4.+
  N13: Bat1.+#0, Bat1.+#2
  N14: Bat1.+#3, U1.IN, U3.input_voltage

custom parts:
  battery_holder_dual_18650: TBH-18650-2A-P dual 18650 battery holder.
  Voltage Regulator -- 3.3 V -- LM1117: LM1117-3.3 Voltage regulator, 3.3 V output. Note that the pinout order is not the same as LM7805 or LM7833.
  NodeMCU V1.0: ESP8266 based NodeMCU
